# Fritzing sketch AtariPaddleAmazon (saved by Fritzing 0.9.6b)

parts:
  J4 = Dagu DGServo 9g header (male) [package=THT]
  J5 = Dagu DGServo 9g header (male) [package=THT]  # not connected
  X3 = DB9 Connector [package=db9]
  X4 = DB9 Connector [package=db9]
  S3 = Round Pushbutton
  S4 = Round Pushbutton
  R3 = Rotary Potentiometer (Large) [maximum_resistance=100kΩ package=THT]
  R4 = Rotary Potentiometer (Large) [maximum_resistance=100kΩ package=THT]

nets:
  N1: J4.p1, X3.5
  N2: J4.p2, X3.4
  N3: X4.3, S3.leg0
  N4: X4.4, S4.leg1
  N5: X4.5, R4.wiper
  N6: X4.7, R3.leg1, R4.leg1
  N7: X4.8, S3.leg1, S4.leg0, R3.leg2
  N8: X4.9, R3.wiper

custom parts:
  Dagu DGServo 9g header (male): Dagu DGServo 9g header (male) This part is a minor variation of the standard three pin header; in schematic view the pins have been labelled to show clearly pulse, Vcc and ground. Plug this header into a breadboard, stripboard or PCB to allow a servo header female connector plug (e.g. on the Dagu DGServo 9g) to be connected to the board.
