# Fritzing sketch AtariPaddlesT2-V6 (saved by Fritzing 0.9.6b)
breadboards: 1

parts:
  Part1 = Arduino Pro Micro (Clone)
  R2 = Resistor [tolerance=±5% resistance=220 package="2512 [SMD]"]
  R3 = Resistor [tolerance=±5% resistance=220 package="2512 [SMD]"]
  R4 = Resistor [tolerance=±5% resistance=220 package="2512 [SMD]"]
  R5 = Resistor [tolerance=±5% resistance=220 package="2512 [SMD]"]
  R6 = Resistor [tolerance=±5% resistance=220 package="2512 [SMD]"]
  R7 = Resistor [tolerance=±5% resistance=220 package="2512 [SMD]"]
  R8 = Resistor [tolerance=±5% resistance=220 package="2512 [SMD]"]
  J3 = Dagu DGServo 9g header (male) [package=THT]
  J4 = Dagu DGServo 9g header (male) [package=THT]
  R10 = Resistor [tolerance=±5% resistance=220 package="2512 [SMD]"]
  R9 = Resistor [tolerance=±5% resistance=220 package="2512 [SMD]"]
  J5 = Dagu DGServo 9g header (male) [package=THT]
  J6 = Dagu DGServo 9g header (male) [package=THT]
  R11 = Resistor [tolerance=±5% resistance=220 package="2512 [SMD]"]
  R12 = Resistor [tolerance=±5% resistance=220 package="2512 [SMD]"]
  R13 = Resistor [tolerance=±5% resistance=220 package="2512 [SMD]"]
  R14 = Resistor [tolerance=±5% resistance=220 package="2512 [SMD]"]  # not connected
  J7 = Dagu DGServo 9g header (male) [package=THT]
  J8 = Dagu DGServo 9g header (male) [package=THT]
  R15 = Resistor [tolerance=±5% resistance=220 package="2512 [SMD]"]
  S1 = Taiway 100-SP-X-T1 SPDT Miniature Toggle Switch [part_number=100-SP-X-T1-0-0-B1-M2 package=THT]

nets:
  N1: Part1.GND, R2.Pin_1, R3.Pin_1, R4.Pin_1, R5.Pin_1, R6.Pin_1, R8.Pin_1, J4.p3, R10.Pin_1, R9.Pin_1, J8.p1, S1.L1
  N2: Part1.D2, R2.Pin_0, J6.p1
  N3: Part1.D3, R3.Pin_0, J6.p2
  N4: Part1.D4, R4.Pin_0, J6.p3
  N5: Part1.D5, R5.Pin_0, J5.p1
  N6: Part1.D6, R6.Pin_0, J5.p2
  N7: Part1.D7, R7.Pin_0
  N8: Part1.D8, R8.Pin_0
  N9: Part1.D9, J3.p2, R9.Pin_0
  N10: Part1.D10, R11.Pin_0, J7.p1
  N11: Part1.D16, R12.Pin_0, J7.p2
  N12: Part1.D14, R13.Pin_0, J7.p3
  N13: Part1.A0, J4.p1
  N14: Part1.A1, J3.p1
  N15: Part1.A2, R15.Pin_0
  N16: Part1.VCC, J4.p2, J5.p3, S1.L2
  N17: J3.p3, R10.Pin_0
  N18: R15.Pin_1, S1.COM

notes:
  23456
  SEL;H;PLAY; X;Y
  987 543
  3-Button right
  4-Button Left
  5-Analog Left
  7-GND pin 5,9
  8-GND pin 3,4
  9-AnalogRight

custom parts:
  Dagu DGServo 9g header (male): Dagu DGServo 9g header (male) This part is a minor variation of the standard three pin header; in schematic view the pins have been labelled to show clearly pulse, Vcc and ground. Plug this header into a breadboard, stripboard or PCB to allow a servo header female connector plug (e.g. on the Dagu DGServo 9g) to be connected to the board.
