# Fritzing sketch AtariPaddles_SPINNER (saved by Fritzing 0.9.6b)
breadboards: 2

parts:
  Part2 = Arduino Micro (Rev3)
  S1 = Round Pushbutton
  S2 = Round Pushbutton
  R1 = Rotary Potentiometer (Large) [maximum_resistance=100kΩ knob_status=50% package=THT]
  R2 = Rotary Potentiometer (Large) [maximum_resistance=100kΩ knob_status=50% package=THT]
  LED1 = LED - 5mm [color="Red (633nm)" current=0.030 package="5 mm [THT]"]
  LED2 = LED - 5mm [color="Red (633nm)" current=0.030 package="5 mm [THT]"]
  LED3 = LED - 5mm [color="Red (633nm)" current=0.030 package="5 mm [THT]"]
  LED4 = LED - 5mm [color="Red (633nm)" current=0.030 package="5 mm [THT]"]
  R3 = Resistor [tolerance=±5% resistance=220 package="2010 [SMD]"]
  R5 = Resistor [tolerance=±5% resistance=220 package="2010 [SMD]"]
  R6 = Resistor [tolerance=±5% resistance=220 package="2010 [SMD]"]
  R4 = Resistor [tolerance=±5% resistance=220 package="2010 [SMD]"]
  R7 = Resistor [tolerance=±5% resistance=220 package="2010 [SMD]"]
  R8 = Resistor [tolerance=±5% resistance=220 package="2010 [SMD]"]
  S4 = Pushbutton [package="[THT]"]
  S5 = Pushbutton [package="[THT]"]
  S6 = Pushbutton [package="[THT]"]
  S7 = Pushbutton [package="[THT]"]
  X1 = DB9 Connector [package=db9]
  X2 = DB9 Connector [package=db9]
  J2 = Dagu DGServo 9g header (male) [package=THT]  # not connected
  J3 = Dagu DGServo 9g header (male) [package=THT]  # not connected
  R9 = Resistor [tolerance=±5% resistance=220 package="2010 [SMD]"]  # not connected
  R10 = Resistor [tolerance=±5% resistance=220 package="2010 [SMD]"]  # not connected
  R11 = Resistor [tolerance=±5% resistance=220 package="2010 [SMD]"]  # not connected
  R12 = Resistor [tolerance=±5% resistance=220 package="2010 [SMD]"]
  S8 = Pushbutton [package="[THT]"]
  R13 = Resistor [tolerance=±5% resistance=220 package="2010 [SMD]"]  # not connected

nets (from the schematic view):
  N1: Part2.D2/SDA, LED4.anode
  N2: Part2.D3/SCL, LED1.anode
  N3: Part2.D4_PWM/A6, LED2.anode
  N4: Part2.D5_PWM, LED3.anode
  N5: Part2.D6_PWM/A7, R8.Pin_0, X2.4
  N6: Part2.D7, R7.Pin_1, X2.3
  N7: Part2.D8_PWM/A8, S7.Pin_3, S7.Pin_4
  N8: Part2.D9_PWM/A9, S6.Pin_3, S6.Pin_4
  N9: Part2.D10_PWM/A10, S4.Pin_3, S4.Pin_4
  N10: Part2.D11_PWM, S5.Pin_3, S5.Pin_4
  N11: Part2.GND, R5.Pin_1, R6.Pin_1, R4.Pin_1, R7.Pin_0, X2.7, R12.Pin_0
  N12: Part2.5V, S4.Pin_1, S4.Pin_2, S5.Pin_1, S5.Pin_2, S6.Pin_1, S6.Pin_2, S7.Pin_1, S7.Pin_2, X2.8
  N13: Part2.A1, X2.5
  N14: Part2.A0, X2.9
  N15: S1.leg0, X1.3
  N16: S1.leg1, S2.leg0, R1.leg2, R2.leg2, X1.8
  N17: S2.leg1, X1.4
  N18: R1.leg1, R2.leg1, X1.7
  N19: R1.wiper, X1.9
  N20: R2.wiper, X1.5
  N21: LED1.cathode, R6.Pin_0
  N22: LED2.cathode, R4.Pin_0
  N23: LED3.cathode, R3.Pin_0
  N24: LED4.cathode, R5.Pin_0
  N25: R3.Pin_1, R8.Pin_1
  N26: S8.Pin_1, S8.Pin_2
  N27: S8.Pin_3, S8.Pin_4

notes:
  3-Button right
  4-Button Left
  5-Analog Left
  7-GND pin 5,9
  8-GND pin 3,4
  9-AnalogRight
  D5432
  BACK VIEW
  5 4 3 2 1
  9 8 7 6
  987 543
  A01-Paddle
  LED
  Pin=2345
  34 Button
  59 Wipper
  8 GND
  7 VCC
  HACK CONNECTION
  8 GND to POTENTIOMETER
  SEL STR X Y H

custom parts:
  Dagu DGServo 9g header (male): Dagu DGServo 9g header (male) This part is a minor variation of the standard three pin header; in schematic view the pins have been labelled to show clearly pulse, Vcc and ground. Plug this header into a breadboard, stripboard or PCB to allow a servo header female connector plug (e.g. on the Dagu DGServo 9g) to be connected to the board.
